# Fritzing sketch manual-wiring (saved by Fritzing 0.9.3b)
breadboards: 1

parts:
  IC2 = IC, DIP package, 28 pins [chip_label=MCP23017]
  IC3 = IC, DIP package, 28 pins [chip_label=MCP23017]
  IC4 = IC, DIP package, 28 pins [chip_label=MCP23017]
  Part1 = Arduino Uno (Rev3)
  R1 = Resistor [tolerance=±5% resistance=10k package=THT]
  IC5 = IC, DIP package, 28 pins [chip_label=MCP23017]
  R2 = Resistor [tolerance=±5% resistance=10k package=THT]

nets:
  N1: IC2.pin10, IC2.pin16, IC2.pin17, IC4.pin17, Part1.GND, IC5.pin10, IC5.pin15, IC5.pin16, IC5.pin17
  N2: IC2.pin12, IC3.pin12, IC4.pin12, Part1.A5/SCL, R1.Pin_0, IC5.pin12
  N3: IC2.pin13, IC3.pin13, IC4.pin13, Part1.A4/SDA, IC5.pin13, R2.Pin_0
  N4: IC2.pin15, IC2.pin18, IC3.pin15, IC3.pin16, IC3.pin17, IC3.pin18, IC4.pin15, IC4.pin16, IC4.pin18, Part1.5V, R1.Pin_1, IC5.pin9, IC5.pin18, R2.Pin_1
